// Logisim project MiniRISCV.circ as structural Verilog: 6 circuits, main circuit main
module main (
  input  in_1,
  input  in_2,
  output [31:0] out_3
);

  wire clock_1_out, decode_black_box_1_p1, decode_black_box_1_p2, decode_black_box_1_p3,
       decode_black_box_1_p6, decode_black_box_1_p7, decode_black_box_1_p8, decode_black_box_1_p9,
       decode_black_box_1_p10, decode_black_box_1_p11, decode_black_box_1_p12, decode_black_box_1_p13,
       decode_black_box_1_p14, decode_black_box_1_p15, decode_black_box_1_p16, decode_black_box_1_p17,
       decode_black_box_1_p18, or_1_out, or_2_out, registerfile_1_p1, risc_vprogramrom_1_p2;
  wire [3:0] decode_black_box_1_p5, multiplexer_3_out;
  wire [4:0] multiplexer_5_out, sa_1_out_2;
  wire [31:0] decode_black_box_1_p4, multiplexer_1_out, multiplexer_2_out, multiplexer_4_out,
       registerfile_1_p7, registerfile_1_p8;

  PC pc_1 (.we(in_1), .clk(clock_1_out), .clr(in_2), .out_4(out_3));
  Clock clock_1 (.out(clock_1_out));
  // RISC_VProgramROM risc_vprogramrom_1: pin names not known; wires that end beside it: out_3, risc_vprogramrom_1_p2, risc_vprogramrom_1_p2
  // Decode_Black_Box decode_black_box_1: pin names not known; wires that end beside it: decode_black_box_1_p1, decode_black_box_1_p2, decode_black_box_1_p3, decode_black_box_1_p4, decode_black_box_1_p5, decode_black_box_1_p6, decode_black_box_1_p7, decode_black_box_1_p8, decode_black_box_1_p9, decode_black_box_1_p10, decode_black_box_1_p11, decode_black_box_1_p12, decode_black_box_1_p13, decode_black_box_1_p14, decode_black_box_1_p15, decode_black_box_1_p16, decode_black_box_1_p17, decode_black_box_1_p18, decode_black_box_1_p10
  or or_1 (or_1_out, decode_black_box_1_p6, decode_black_box_1_p7, decode_black_box_1_p8, decode_black_box_1_p9, decode_black_box_1_p11, decode_black_box_1_p13, decode_black_box_1_p14, decode_black_box_1_p15, decode_black_box_1_p16);
  // RegisterFile registerfile_1: pin names not known; wires that end beside it: registerfile_1_p1, clock_1_out, 1'b1, decode_black_box_1_p3, decode_black_box_1_p1, decode_black_box_1_p2, registerfile_1_p7, registerfile_1_p8
  or or_2 (or_2_out, decode_black_box_1_p17, decode_black_box_1_p18);
  Multiplexer #(.width(32), .enable("false")) multiplexer_1 (
    .in0(registerfile_1_p7), .in1(decode_black_box_1_p4), .out(multiplexer_1_out), .sel(or_2_out));
  Multiplexer #(.width(32), .enable("false")) multiplexer_2 (
    .in0(registerfile_1_p8), .in1(decode_black_box_1_p4), .out(multiplexer_2_out), .sel(or_1_out));
  Multiplexer #(.width(4), .enable("false")) multiplexer_3 (
    .in0(decode_black_box_1_p5), .in1(4'b0111), .out(multiplexer_3_out), .sel(decode_black_box_1_p17));
  Multiplexer #(.width(32), .enable("false")) multiplexer_4 (
    .in0(multiplexer_2_out), .in1(out_3), .out(multiplexer_4_out), .sel(decode_black_box_1_p18));
  SA sa_1 (.SA_32(multiplexer_2_out), .out_2(sa_1_out_2));
  Multiplexer #(.width(5), .enable("false")) multiplexer_5 (
    .in0(sa_1_out_2), .in1(5'b01100), .out(multiplexer_5_out), .sel(decode_black_box_1_p17));
  // Comparator_Black_Box comparator_black_box_1: pin names not known
  // ALU alu_1: pin names not known; wires that end beside it: multiplexer_1_out, multiplexer_4_out, multiplexer_3_out, multiplexer_5_out, registerfile_1_p1

  // Notes on the sheet:
  //   contents of risc_vprogramrom_1 (hex, n*v repeats v):
  //   lui t1, 1 lui t2, 2  add t3, t1, t0 # t2 = t1 +t0 xor t4, t1, t2 or t5, t1, t2 auipc a0, 0 sub t0,
  //   t1, t2 # t0 = t1 - t2
endmodule

module PC (
  input  we,
  input  clk,
  input  clr,
  output [31:0] out_4
);

  wire incrementer_1_p2, incrementer_2_p1, incrementer_3_p1;
  wire [31:0] incrementer_4_p1;

  Register #(.width(32)) clk_in (.D(incrementer_4_p1), .en(we), .clk(clk), .Q(out_4), .clr(clr));
  // Incrementer #(.width(32)) incrementer_1: pin names not known; wires that end beside it: out_4, incrementer_1_p2, incrementer_1_p2
  // Incrementer #(.width(32)) incrementer_2: pin names not known; wires that end beside it: incrementer_2_p1, incrementer_2_p1
  // Incrementer #(.width(32)) incrementer_3: pin names not known; wires that end beside it: incrementer_3_p1, incrementer_3_p1
  // Incrementer #(.width(32)) incrementer_4: pin names not known; wires that end beside it: incrementer_4_p1
endmodule

module Control (
  input  [31:0] inst,
  output [4:0] rs1,
  output [4:0] rs2,
  output [4:0] rd,
  output [31:0] imm,
  output useImm,
  output [3:0] ALUop
);

  // Decode_Black_Box decode_black_box_1: pin names not known; wires that end beside it: inst, rs1, rs2, rd, imm, useImm, ALUop
endmodule

module SA (
  input  [31:0] SA_32,
  output [4:0] out_2
);


  assign out_2 = SA_32[4:0];
endmodule

module mem (
  input  store,
  input  [3:0] sel_bit,
  input  load,
  input  clear
);

  RAM ram_1 ();  // open: addr, data, sel, clk, ld, clr
endmodule

module rewire (
  input  i1,
  input  i2,
  input  i3,
  input  i4,
  output o1,
  output o2,
  output o3,
  output o4
);

  wire and_1_out, and_2_out, and_3_out, and_4_out, and_5_out, and_6_out, and_7_out, and_8_out, and_9_out,
       and_10_out, and_11_out, not_1_out, not_2_out, not_3_out, not_4_out, not_5_out, not_6_out, not_7_out,
       not_8_out, not_9_out, not_10_out;

  not not_1 (not_1_out, i1);
  and and_1 (and_1_out, not_1_out, not_2_out);
  not not_2 (not_2_out, i4);
  and and_2 (and_2_out, i1, not_3_out);
  not not_3 (not_3_out, i3);
  and and_3 (and_3_out, i2, i4);
  and and_4 (and_4_out, i1, not_4_out);
  not not_4 (not_4_out, i3);
  and and_5 (and_5_out, i1, i2);
  not not_5 (not_5_out, i1);
  and and_6 (and_6_out, not_5_out, i2, not_6_out);
  not not_6 (not_6_out, i4);
  and and_7 (and_7_out, i1, not_7_out);
  not not_7 (not_7_out, i2);
  and and_8 (and_8_out, i1, i3);
  not not_8 (not_8_out, i3);
  and and_9 (and_9_out, not_8_out, i4);
  not not_9 (not_9_out, i1);
  and and_10 (and_10_out, not_9_out, i3, not_10_out);
  not not_10 (not_10_out, i4);
  and and_11 (and_11_out, i1, i4);
  or or_1 (o1, and_1_out, and_2_out);
  or or_2 (o2, and_3_out, and_4_out, and_5_out);
  or or_3 (o3, and_6_out, and_7_out, and_8_out);
  or or_4 (o4, and_9_out, and_10_out, and_11_out);
endmodule
